// Logisim project digitalclock.circ as structural Verilog: 1 circuit, main circuit main
module main (
  input  in_1,
  input  in_2
);

  wire and_1_out, and_2_out, and_3_out, and_4_out, and_5_out, clock_1_out, comparator_1_eq, comparator_2_eq,
       counter_3_carry, D0, D1, H_plus, M_plus, not_1_out, or_1_out, or_2_out, shift_register_1_out;
  wire [3:0] main_1_y0, main_1_y1, main_1_y2, main_1_y3;
  wire [4:0] AHour, Hour;
  wire [5:0] AMin, Min;

  Button button_1 (.out(M_plus));
  Button button_2 (.out(H_plus));
  Counter #(.width(6), .max('h3c)) counter_1 (.carry(D0), .clk(clock_1_out), .clr(D0));  // open: load, D, count, Q
  Clock clock_1 (.out(clock_1_out));
  and and_1 (and_1_out, M_plus, ~in_1);  // AND_Gate
  and and_2 (and_2_out, H_plus, ~in_1);  // AND_Gate
  Counter #(.width(6), .max('h3c)) counter_2 (.Q(Min), .carry(D1), .clk(or_1_out), .clr(D1));  // open: load, D, count
  or or_1 (or_1_out, and_1_out, D0);
  Counter #(.width(5), .max('h18)) counter_3 (
    .Q(Hour), .carry(counter_3_carry), .clk(or_2_out), .clr(counter_3_carry));  // open: load, D, count
  or or_2 (or_2_out, and_2_out, D1);
  Comparator #(.width(6)) comparator_1 (.a(Min), .b(AMin), .eq(comparator_1_eq));  // open: gt, lt
  Comparator #(.width(5)) comparator_2 (.a(Hour), .b(AHour), .eq(comparator_2_eq));  // open: gt, lt
  Shift_Register #(.length(1)) shift_register_1 (
    .in(1'b1), .clk(and_3_out), .out(shift_register_1_out), .clr(not_1_out));  // open: shift, load, d0, q0
  and and_3 (and_3_out, comparator_1_eq, comparator_2_eq, in_2);
  not not_1 (not_1_out, in_2);
  Hex_Digit_Display hex_digit_display_1 (.value(main_1_y2));  // open: dp
  hexdisplay_main main_1 (
    .Y0(main_1_y0), .Y1(main_1_y1), .Y2(main_1_y2), .Y3(main_1_y3), .X0(Min), .X1(Hour), .Set_Larm(in_1),
    .Z0(AMin), .Z1(AHour), .Alarm(in_2));
  Hex_Digit_Display hex_digit_display_2 (.value(main_1_y3));  // open: dp
  LED led_1 (.in(shift_register_1_out));
  Hex_Digit_Display hex_digit_display_3 (.value(main_1_y0));  // open: dp
  Hex_Digit_Display hex_digit_display_4 (.value(main_1_y1));  // open: dp
  and and_4 (and_4_out, M_plus, in_1);
  and and_5 (and_5_out, H_plus, in_1);
  Counter #(.width(6), .max('h3c)) counter_4 (.Q(AMin), .clk(and_4_out));  // open: load, D, count, carry, clr
  Counter #(.width(5), .max('h18)) counter_5 (.Q(AHour), .clk(and_5_out));  // open: load, D, count, carry, clr

  // Other names for the same wires on the sheet: Alarm = in_2; Set_Larm = in_1
endmodule
