// Logisim project hexdisplay.circ as structural Verilog: 1 circuit, main circuit main
module main (
  input  [5:0] X0,
  input  [4:0] X1,
  input  [5:0] Z0,
  input  [4:0] Z1,
  input  Set_Larm,
  input  Alarm,
  output [3:0] Y0,
  output [3:0] Y1,
  output [3:0] Y2,
  output [3:0] Y3
);

  wire [4:0] R1;
  wire [4:4] divider_2_out, divider_2_rem;
  wire [5:0] R0;
  wire [5:4] divider_1_out, divider_1_rem;

  Multiplexer #(.width(6), .enable("false")) multiplexer_1 (.in0(X0), .in1(Z0), .out(R0), .sel(Set_Larm));
  Divider #(.width(6)) divider_1 (
    .a(R0), .b(6'b001010), .out({divider_1_out, Y1}), .rem({divider_1_rem, Y0}));  // open: upper
  Multiplexer #(.width(5), .enable("false")) multiplexer_2 (.in0(X1), .in1(Z1), .out(R1), .sel(Set_Larm));
  Divider #(.width(5)) divider_2 (
    .a(R1), .b(5'b01010), .out({divider_2_out[4], Y3}), .rem({divider_2_rem[4], Y2}));  // open: upper
endmodule
